# Fritzing sketch Untitled Sketch.. (saved by Fritzing 0.9.3b)
breadboards: 2

parts:
  S1 = Momentary Switch [package=ksa_sealed_tac_switch]
  S2 = Momentary Switch [package=ksa_sealed_tac_switch]
  R3 = Resistor [tolerance=±5% resistance=220 package=THT]
  R4 = Resistor [tolerance=±5% resistance=220 package=THT]
  Part1 = Arduino Nano (Rev3.0)
  LED6 = LED - 3mm [color="Red (633nm)" package="3 mm [THT]"]  # not connected
  LED7 = LED - 3mm [color="Red (633nm)" package="3 mm [THT]"]  # not connected
  LED8 = LED - 3mm [color="Red (633nm)" package="3 mm [THT]"]  # not connected
  LED10 = LED - 3mm [color="Red (633nm)" package="3 mm [THT]"]  # not connected
  LED9 = LED - 3mm [color="Red (633nm)" package="3 mm [THT]"]  # not connected
  S3 = Momentary Switch [package=ksa_sealed_tac_switch]  # not connected
  LED11 = LED - 3mm [color="Red (633nm)" package="3 mm [THT]"]
  LED15 = LED - 3mm [color="Red (633nm)" package="3 mm [THT]"]
  LED14 = LED - 3mm [color="Red (633nm)" package="3 mm [THT]"]
  LED16 = LED - 3mm [color="Red (633nm)" package="3 mm [THT]"]
  U7 = RF-LINK_TX [package=rf-link_tx]
  U8 = RF-LINK_RX [package=rf-link_rx]  # not connected

nets:
  N1: S1.3, R3.Pin_1, Part1.D6
  5V: S1.4, S2.4, Part1.RESET, Part1.5V, U7.+5V
  N2: S2.3, R4.Pin_1, Part1.D7
  GND: R3.Pin_0, R4.Pin_0, Part1.GND, LED11.cathode, LED15.cathode, LED14.cathode, LED16.cathode, U7.GND
  N3: Part1.D2, LED16.anode
  N4: Part1.D3, LED11.anode
  N5: Part1.D4, LED14.anode
  N6: Part1.D5, LED15.anode
  N7: Part1.D10, U7.DATA

custom parts:
  RF-LINK_TX: Common RF transmitter of the 315.00Mhz varity
  RF-LINK_RX: RF Link receivers- WRL-8947, 8948, 8949, 8950
