# Fritzing sketch Untitled Sketch (saved by Fritzing 0.9.3b)
breadboards: 1

parts:
  S2 = Momentary Switch [package=ksa_sealed_tac_switch]
  Part1 = Arduino Nano (Rev3.0)
  LED8 = LED - 3mm [color="Red (633nm)" package="3 mm [THT]"]
  U7 = RF-LINK_RX [package=rf-link_rx]  # not connected
  U9 = RF-LINK_RX [package=rf-link_rx]
  LED16 = LED - 3mm [color="Red (633nm)" package="3 mm [THT]"]
  LED17 = LED - 3mm [color="Red (633nm)" package="3 mm [THT]"]
  LED18 = LED - 3mm [color="Red (633nm)" package="3 mm [THT]"]
  LED19 = LED - 3mm [color="Red (633nm)" package="3 mm [THT]"]
  R5 = Resistor [tolerance=±5% resistance=220 package=THT]

nets:
  N1: S2.1, Part1.D7, R5.Pin_1
  N2: S2.2, Part1.5V
  N3: Part1.D2, U9.Data
  N4: Part1.D3, LED18.anode
  N5: Part1.D4, LED8.anode
  N6: Part1.D5, LED17.anode
  N7: Part1.D6, LED16.anode
  N8: Part1.D8, LED19.anode
  N9: LED8.cathode, U9.GND, LED16.cathode, LED17.cathode, LED18.cathode, LED19.cathode, R5.Pin_0

custom parts:
  RF-LINK_RX: RF Link receivers- WRL-8947, 8948, 8949, 8950
